// Logisim project Project3.circ as structural Verilog: 1 circuit, main circuit main
module main (
  input  [7:0] IR_8_15
);

  wire Enable_2A, Enable_2B, Enable_2C, Enable_MuxA, Enable_MuxB, Enable_MuxC, EnableRAM, L_H, Load, MuxCSel,
       Read;
  wire [1:0] FunSel_2A, FunSel_2B, FunSel_2C, MuxASel, MuxBSel, OuBSel, OutASel, OutCSel, OutDSel;
  wire [2:0] RegSel_2B;
  wire [3:0] FunSel_ALU, RegSel_2A;
  wire [7:0] IR, main_2_outa, main_2_outb, main_3_outalu, main_4_outc, main_4_outd, multiplexer_1_out,
       multiplexer_2_out, multiplexer_3_out, ram_1_data;

  Multiplexer #(.select(2), .width(8)) multiplexer_1 (
    .in0(IR), .in1(ram_1_data), .in2(main_4_outc), .in3(main_3_outalu), .out(multiplexer_1_out),
    .sel(MuxASel), .en(Enable_MuxA));
  PART_2C_main main_1 (
    .EN(Enable_2C), .Funsel(FunSel_2C), .IN(ram_1_data), .L_H(L_H), .OUT({IR_8_15, IR}));  // open: CLK
  PART_2A_main main_2 (
    .I(multiplexer_1_out), .OutA(main_2_outa), .OutB(main_2_outb), .clk(Enable_2A), .OutASel(OutASel),
    .OutBSel(OuBSel), .FunSel(FunSel_2A), .RegSel(RegSel_2A));
  Multiplexer #(.width(8)) multiplexer_2 (
    .in0(multiplexer_1_out), .in1(main_2_outa), .out(multiplexer_2_out), .sel(MuxCSel), .en(Enable_MuxC));
  Multiplexer #(.select(2), .width(8)) multiplexer_3 (
    .in1(IR), .in2(ram_1_data), .in3(main_3_outalu), .out(multiplexer_3_out), .sel(MuxBSel), .en(Enable_MuxB));  // open: in0
  Part1_main main_3 (
    .A(multiplexer_2_out), .B(main_2_outb), .FunSel(FunSel_ALU), .OutALU(main_3_outalu));  // open: CLK, OutFlag__ZCNO
  PART_2B_main main_4 (
    .I(multiplexer_3_out), .OutC(main_4_outc), .OutD(main_4_outd), .OutCSel(OutCSel), .OutDSel(OutDSel),
    .FunSel(FunSel_2B), .EN(Enable_2B), .RegSel(RegSel_2B));  // open: CLK
  RAM #(.bus("separate")) ram_1 (
    .addr(main_4_outd), .din(main_3_outalu), .data(ram_1_data), .str(Load), .sel(EnableRAM), .ld(Read));  // open: clk, clr
  // also tied to GND on the sheet: {main_4_outd[0], main_4_outd[1], main_4_outd[2], main_4_outd[3], main_4_outd[6], main_4_outd[7]}
  // also tied to VCC on the sheet: {main_4_outd[4], main_4_outd[5]}

  // Other names for the same wires on the sheet: IR[15:8] = IR_8_15
endmodule
