// Logisim project sequencer.circ as structural Verilog: 1 circuit, main circuit main
module main (
  input  CLK,
  input  [8:0] MAP,
  output [5:0] MicroOp
);

  wire and_1_out, and_2_out, and_3_out, buffer_1_out, multiplexer_2_out, undriven;
  wire [1:0] or_1_out;
  wire [8:0] adder_1_out, main_1_output, main_2_output, multiplexer_1_out, rom_1_data;
  wire [12:10] rom_1_data_2;

  Adder #(.width(9)) adder_1 (.a(main_2_output), .b({9{1'b1}}), .out(adder_1_out));  // open: cin, cout
  _9_BIT_D_FLIP_FLOP_main main_1 (.CLK(CLK), .EN(and_1_out), .INPUT(adder_1_out), .OUTPUT(main_1_output));
  Multiplexer #(.select(2), .width(9)) multiplexer_1 (
    .in0(MAP), .in1(adder_1_out), .in2(main_1_output), .in3(rom_1_data), .out(multiplexer_1_out),
    .sel(or_1_out));  // open: en
  Multiplexer #(.select(2)) multiplexer_2 (
    .in0(1'b1), .in1(undriven), .out(multiplexer_2_out), .sel(rom_1_data_2[12:11]));  // open: in2, in3, en
  and and_1 (and_1_out, or_1_out[0], rom_1_data_2[10], multiplexer_2_out);
  or or_1 (or_1_out[1], and_2_out, and_3_out);
  _9_BIT_D_FLIP_FLOP_main main_2 (.CLK(CLK), .INPUT(multiplexer_1_out), .OUTPUT(main_2_output));  // open: EN
  and and_2 (and_2_out, or_1_out[0], rom_1_data_2[10]);
  and and_3 (and_3_out, buffer_1_out, multiplexer_2_out);
  buf buffer_1 (buffer_1_out, or_1_out[0]);
  ROM #(.addrWidth(9), .dataWidth(19)) rom_1 (
    .addr(main_2_output), .data({MicroOp, rom_1_data_2, or_1_out[0], rom_1_data}));  // open: sel

  // Notes on the sheet:
  //   SBR
endmodule
